// Logisim project 5.circ as structural Verilog: 1 circuit, main circuit main
module main (
  output [7:0] out_1,
  output [15:0] Out1,
  output halt,
  output [15:0] out_4,
  output [3:0] out_5
);

  wire clock_1_out;
  wire [7:0] adder_1_out;

  Clock clock_1 (.out(clock_1_out));
  Adder adder_1 (.a(8'h1), .b(out_1), .out(adder_1_out));  // open: cin, cout
  Register register_1 (.D(adder_1_out), .clk(clock_1_out), .Q(out_1));  // open: en, clr
  ROM #(.dataWidth(16)) rom_1 (.addr(out_1), .data(out_4));
  Comparator comparator_1 (.a(out_1), .b(8'h7), .eq(halt));  // open: gt, lt
  ROM #(.dataWidth(4)) rom_2 (.addr(out_1), .data(out_5));
  // rotr rotr_1: pin names not known; wires that end beside it: out_4, out_5, Out1

  // Other names for the same wires on the sheet: A[15:0] = out_4; B[3:0] = out_5; Test[7:0] = out_1

  // Notes on the sheet:
  //   contents of rom_1 (hex, n*v repeats v):
  //   8*1
  //   Your rotr circuit must fit here!
  //   contents of rom_2 (hex, n*v repeats v):
  //   1 2 4 8 3 5 9 f
  //   There should be no red or blue wires, and the result should not be all X's
endmodule
